# Fritzing sketch IDE2019 (saved by Fritzing 0.9.3b)
breadboards: 1

parts:
  Part1 = Arduino Pro Mini v13
  U2 = ESP8266 WiFi Module [part_number=ESP8266]
  Part2 = InvenSense MPU6050
  S1 = Pushbutton [package="[THT]"]
  D2 = Rectifier Diode [part_number=1N4001 package="300 mil [THT]"]
  R1 = Resistor [tolerance=±5% resistance=220 package="0805 [SMD]"]
  C1 = Ceramic Capacitor [capacitance=100nF package="200 mil [THT, multilayer]"]
  R2 = Resistor [tolerance=±5% resistance=220 package="0805 [SMD]"]
  VCC1 = Battery block 9V

nets:
  VCC: Part1.VCC, Part2.VCC, R1.Pin_1
  N1: Part1.A4, Part2.SDA
  N2: Part1.A5, Part2.SCL
  GND: Part1.GND, U2.GND, Part2.GND, S1.Pin_1, S1.Pin_2, D2.anode, R1.Pin_0, C1.0, R2.Pin_1, VCC1.-
  N3: Part1.D11_PWM/MOSI, U2.GPIO_2
  N4: Part1.D2, Part2.INT
  N5: S1.Pin_3, S1.Pin_4
  N6: D2.cathode, C1.1, R2.Pin_0

custom parts:
  ESP8266 WiFi Module: Generic WiFi Module based on the ESP8266 with onboard PCB antenna and UART communications
